# Fritzing sketch UART (saved by Fritzing 0.8.7b)

parts:
  Raspberry_Pi_B_rev2 = Raspberry Pi B rev2
  Nano2 = Arduino Nano v2.3
  Part2 = Logic Level Converter

nets:
  GND: Raspberry_Pi_B_rev2.GND, Nano2.GND, Nano2.D2, Part2.GND
  N1: Raspberry_Pi_B_rev2.GPIO_14, Part2.RX2_HV
  N2: Raspberry_Pi_B_rev2.GPIO_15, Part2.TX2_HV
  N3: Nano2.D1TX, Part2.TX2_LV
  N4: Nano2.D0RX, Nano2.RST, Part2.RX2_LV
